# Fritzing sketch RX shema (saved by Fritzing 0.9.4)

parts:
  Parça2 = NRF24L01+ Breakout Board
  Parça3 = Arduino Uno (Rev3)

nets:
  GND: Parça2.GND, Parça3.GND
  VCC: Parça2.VCC, Parça3.3V3
  N1: Parça2.CE, Parça3.D9_PWM
  N2: Parça2.CS, Parça3.D10_PWM/SS
  N3: Parça2.SCK, Parça3.D13/SCK
  N4: Parça2.MOSI, Parça3.D11_PWM/MOSI
  N5: Parça2.MISO, Parça3.D12/MISO
