# Fritzing sketch TX shema (saved by Fritzing 0.9.4)

parts:
  Parça1 = Arduino Nano (Rev3.0)
  Parça2 = NRF24L01+ Breakout Board
  GY-NEO6MV3 = SUP500F [package=sup500f]

nets:
  GND: Parça1.GND, Parça2.GND, GY-NEO6MV3.GND
  N1: Parça1.D3, GY-NEO6MV3.RX-I
  N2: Parça1.D4, GY-NEO6MV3.TX-O
  N3: Parça1.D9, Parça2.CE
  N4: Parça1.D10, Parça2.CS
  N5: Parça1.D11/MOSI, Parça2.MOSI
  N6: Parça1.D12/MISO, Parça2.MISO
  5V: Parça1.5V, GY-NEO6MV3.VCC
  3V3: Parça1.3V3, Parça2.VCC
  N7: Parça1.D13/SCK, Parça2.SCK
